// Logisim project volumen_leds.circ as structural Verilog
module deco_leds (
  input  A,
  input  B,
  input  C,
  output led1,
  output led2,
  output led3,
  output led4,
  output led5,
  output led6,
  output led7
);

  wire and_3_out, and_4_out, and_5_out;

  and and_1 (led1, A, B, C);
  and and_2 (led2, A, B);
  and and_3 (and_3_out, A, C);
  and and_4 (and_4_out, A, B);
  and and_5 (and_5_out, B, C);
  or or_1 (led6, B, A);
  or or_2 (led7, C, B, A);
  or or_3 (led3, and_3_out, and_4_out);
  or or_4 (led5, and_5_out, A);

  assign led4 = A;
endmodule
